// Logisim project PLDs.circ as structural Verilog: 20 circuits, main circuit test
module test (
);


  // Notes on the sheet:
  //   Cory Mollenhour
  //   CLA 9
endmodule

module PC_BUS (
  input  t0,
  input  t2,
  output PC_BUS
);

  or or_1 (PC_BUS, t0, t2);
endmodule

module AR_LD (
  input  t0,
  input  t2,
  input  t4,
  input  clock,
  input  d1,
  input  d2,
  output AR_LD
);

  wire and_1_out, and_2_out, and_3_out, not_1_out, not_2_out, not_3_out, or_1_out;

  not not_1 (not_1_out, clock);
  not not_2 (not_2_out, clock);
  or or_1 (or_1_out, d1, d2);
  not not_3 (not_3_out, clock);
  and and_1 (and_1_out, t0, not_1_out);
  and and_2 (and_2_out, t2, not_2_out);
  and and_3 (and_3_out, t4, or_1_out, not_3_out);
  or or_2 (AR_LD, and_1_out, and_2_out, and_3_out);
endmodule

module PC_LD (
  input  t4,
  input  clock,
  input  d5,
  input  d6,
  input  z,
  output PC_LD
);

  wire and_1_out, not_1_out, or_1_out;

  and and_1 (and_1_out, z, d6);
  or or_1 (or_1_out, d5, and_1_out);
  not not_1 (not_1_out, clock);
  and and_2 (PC_LD, t4, or_1_out, not_1_out);
endmodule

module PC_INC (
  input  t1,
  input  t3,
  input  clock,
  input  d1,
  input  d2,
  input  d6,
  input  z,
  output PC_INC
);

  wire and_1_out, and_2_out, not_1_out, not_2_out, or_1_out, or_2_out;

  not not_1 (not_1_out, z);
  and and_1 (and_1_out, not_1_out, d6);
  or or_1 (or_1_out, d1, d2, and_1_out);
  and and_2 (and_2_out, t3, or_1_out);
  or or_2 (or_2_out, t1, and_2_out);
  not not_2 (not_2_out, clock);
  and and_3 (PC_INC, or_2_out, not_2_out);
endmodule

module DR_LD (
  input  t1,
  input  t3,
  input  t5,
  input  clock,
  input  d1,
  input  d2,
  input  d5,
  input  d6,
  input  z,
  output DR_LD
);

  wire and_1_out, and_2_out, and_3_out, not_1_out, or_1_out, or_2_out, or_3_out;

  and and_1 (and_1_out, z, d6);
  or or_1 (or_1_out, d1, d2, d5, and_1_out);
  or or_2 (or_2_out, d1, d2);
  and and_2 (and_2_out, t3, or_1_out);
  and and_3 (and_3_out, t5, or_2_out);
  or or_3 (or_3_out, t1, and_2_out, and_3_out);
  not not_1 (not_1_out, clock);
  and and_4 (DR_LD, or_3_out, not_1_out);
endmodule

module DR_BUS (
  input  t4,
  input  t6,
  input  d1,
  input  d2,
  input  d5,
  input  d6,
  input  z,
  output DR_BUS
);

  wire and_1_out, and_2_out, and_3_out, or_1_out, or_2_out;

  and and_1 (and_1_out, z, d6);
  or or_1 (or_1_out, d1, d2, d5, and_1_out);
  or or_2 (or_2_out, d1, d2);
  and and_2 (and_2_out, t4, or_1_out);
  and and_3 (and_3_out, t6, or_2_out);
  or or_3 (DR_BUS, and_2_out, and_3_out);
endmodule

module R_LD (
  input  t3,
  input  clock,
  input  d3,
  output R_LD
);

  wire not_1_out;

  not not_1 (not_1_out, clock);
  and and_1 (R_LD, t3, d3, not_1_out);
endmodule

module R_BUS (
  input  t3,
  input  d4,
  input  d8,
  input  d9,
  input  d12,
  input  d13,
  output R_BUS
);

  wire or_1_out;

  or or_1 (or_1_out, d4, d8, d9, d12, d13);
  and and_1 (R_BUS, t3, or_1_out);
endmodule

module S_LD (
  input  t3,
  input  clock,
  input  d0,
  output S_LD
);

  wire not_1_out;

  not not_1 (not_1_out, clock);
  and and_1 (S_LD, t3, d0, not_1_out);
endmodule

module ACC_CLR (
  input  t3,
  input  d11,
  output ACC_CLR
);

  and and_1 (ACC_CLR, t3, d11);
endmodule

module ACC_LD (
  input  t3,
  input  t6,
  input  clock,
  input  d1,
  input  d4,
  input  d8,
  input  d9,
  input  d10,
  input  d12,
  input  d13,
  input  d14,
  input  d15,
  output ACC_LD
);

  wire and_1_out, and_2_out, not_1_out, or_1_out, or_2_out;

  or or_1 (or_1_out, d4, d8, d9, d10, d12, d13, d14, d15);
  and and_1 (and_1_out, t3, or_1_out);
  or or_2 (or_2_out, and_1_out, and_2_out);
  and and_2 (and_2_out, t6, d1);
  not not_1 (not_1_out, clock);
  and and_3 (ACC_LD, or_2_out, not_1_out);
endmodule

module ACC_BUS (
  input  t3,
  input  t5,
  input  d2,
  input  d3,
  input  d7,
  output ACC_BUS
);

  wire and_1_out, and_2_out, or_1_out;

  or or_1 (or_1_out, d3, d7);
  and and_1 (and_1_out, t5, d2);
  and and_2 (and_2_out, t3, or_1_out);
  or or_2 (ACC_BUS, and_1_out, and_2_out);
endmodule

module ALU_SEL (
  input  d1,
  input  d4,
  input  d9,
  input  d10,
  input  d12,
  input  d13,
  input  d14,
  input  d15,
  output S2,
  output S1,
  output S0
);

  or or_1 (S2, d12, d13, d14, d15);
  or or_2 (S1, d1, d4, d10, d14, d15);
  or or_3 (S0, d1, d4, d9, d13, d15);
endmodule

module Z_LD (
  input  clock,
  output Z_LD
);

  wire not_1_out;

  not not_1 (not_1_out, clock);
  buf and_1 (Z_LD, not_1_out);  // AND_Gate
endmodule

module OUTR_LD (
  input  t3,
  input  clock,
  input  d7,
  output OUTR_LD
);

  wire not_1_out;

  not not_1 (not_1_out, clock);
  and and_1 (OUTR_LD, t3, d7, not_1_out);
endmodule

module SC_CLR (
  input  t4,
  input  t5,
  input  t7,
  input  d0,
  input  d1,
  input  d2,
  input  d5,
  input  d6,
  input  z,
  output SC_CLR
);

  wire and_1_out, and_2_out, and_3_out, and_4_out, nor_1_out, or_1_out;

  and and_1 (and_1_out, z, d6);
  and and_2 (and_2_out, z, d6);
  nor nor_1 (nor_1_out, d1, d2, d5, and_1_out);
  or or_1 (or_1_out, d5, and_2_out);
  and and_3 (and_3_out, t4, nor_1_out);
  and and_4 (and_4_out, t5, or_1_out);
  or or_2 (SC_CLR, d0, and_3_out, and_4_out, t7);
endmodule

module IR_LD (
  input  t2,
  input  clock,
  output IR_LD
);

  wire not_1_out;

  not not_1 (not_1_out, clock);
  and and_1 (IR_LD, t2, not_1_out);
endmodule

module RAM_RW (
  input  t1,
  input  t3,
  input  t5,
  input  d1,
  input  d2,
  input  d5,
  input  d6,
  input  z,
  output RAM_RW
);

  wire and_1_out, and_2_out, and_3_out, or_1_out;

  and and_1 (and_1_out, z, d6);
  or or_1 (or_1_out, d1, d2, d5, and_1_out);
  or or_2 (RAM_RW, t1, and_2_out, and_3_out);
  and and_2 (and_2_out, t3, or_1_out);
  and and_3 (and_3_out, t5, d1);
endmodule

module RAM_EN (
  input  t1,
  input  t3,
  input  t5,
  input  t6,
  input  d1,
  input  d2,
  input  d5,
  input  d6,
  input  z,
  output RAM_EN
);

  wire and_1_out, and_2_out, and_3_out, and_4_out, or_1_out;

  and and_1 (and_1_out, z, d6);
  or or_1 (or_1_out, d1, d2, d5, and_1_out);
  and and_2 (and_2_out, d2, t6);
  and and_3 (and_3_out, t3, or_1_out);
  and and_4 (and_4_out, t5, d1);
  or or_2 (RAM_EN, and_2_out, t1, and_3_out, and_4_out);
endmodule
