// Logisim project RSC.circ as structural Verilog: 10 circuits, main circuit Arith_U
// AU
module Arith_U (
  input  [31:0] A,
  input  [31:0] B,
  input  S1,
  input  S0,
  output [31:0] AU_out
);

  wire and_1_out, not_2_out;
  wire [31:0] adder_1_out, multiplexer_1_out, not_1_out;

  assign not_1_out = ~B;  // NOT_Gate not_1, 32 bits wide
  Multiplexer #(.select(2), .width(32), .enable("false")) multiplexer_1 (
    .in0(not_1_out), .in1(B), .in2({32{1'b0}}), .in3(B), .out(multiplexer_1_out), .sel({S1, S0}));
  Adder #(.width(32)) adder_1 (.a(A), .b(multiplexer_1_out), .out(adder_1_out), .cin(not_2_out));  // open: cout
  and and_1 (and_1_out, S1, S0);
  not not_2 (not_2_out, S0);
  Multiplexer #(.width(32), .enable("false")) multiplexer_2 (
    .in0(adder_1_out), .in1(multiplexer_1_out), .out(AU_out), .sel(and_1_out));

  // Notes on the sheet:
  //   Cory Mollenhour
  //   CLA6
endmodule

// LU
module Logic_U (
  input  [31:0] A,
  input  [31:0] B,
  input  S1,
  input  S0,
  output [31:0] Logic_Out
);

  wire [31:0] and_1_out, not_1_out, or_1_out, shifter_1_out;

  assign and_1_out = A & B;  // AND_Gate and_1, 32 bits wide
  assign or_1_out = A | B;  // OR_Gate or_1, 32 bits wide
  Shifter #(.width(32), .shift("ar")) shifter_1 (.in(A), .\dist (5'b00001), .out(shifter_1_out));
  assign not_1_out = ~A;  // NOT_Gate not_1, 32 bits wide
  Multiplexer #(.select(2), .width(32), .enable("false")) multiplexer_1 (
    .in0(and_1_out), .in1(or_1_out), .in2(shifter_1_out), .in3(not_1_out), .out(Logic_Out), .sel({S1, S0}));

  // Notes on the sheet:
  //   Cory Mollenhour
  //   CLA6
endmodule

module ALU (
  input  [31:0] A,
  input  [31:0] B,
  input  S2,
  input  S1,
  input  S0,
  output [31:0] ALU_Out
);

  wire [31:0] arith_u_1_au_out, logic_u_1_logic_out;

  Arith_U arith_u_1 (.A(A), .B(B), .S1(S1), .S0(S0), .AU_out(arith_u_1_au_out));
  Logic_U logic_u_1 (.A(A), .B(B), .S1(S1), .S0(S0), .Logic_Out(logic_u_1_logic_out));
  Multiplexer #(.width(32)) multiplexer_1 (
    .in0(arith_u_1_au_out), .in1(logic_u_1_logic_out), .out(ALU_Out), .sel(S2));  // open: en

  // Notes on the sheet:
  //   Cory Mollenhour
  //   CLA6
endmodule

module SC (
  input  Clock,
  input  Clear,
  output [2:0] SEQ_out
);

  wire [2:0] adder_1_out;

  Adder #(.width(3)) adder_1 (.a(3'b001), .b(SEQ_out), .out(adder_1_out));  // open: cin, cout
  Register #(.width(3)) register_1 (.D(adder_1_out), .Q(SEQ_out), .clk(Clock), .clr(Clear));  // open: en

  // Notes on the sheet:
  //   Cory Mollenhour
  //   Closed Lab 7
endmodule

module Decoder (
  input  [31:0] IR_In,
  output [15:0] D_Out,
  output [3:0] Debug_Instruction
);

  wire or_1_out;
  wire [3:0] or_2_out;
  wire [15:0] decoder_1_out0;

  Multiplexer #(.width(16), .enable("false")) multiplexer_1 (
    .in0(decoder_1_out0), .in1({16{1'b0}}), .out(D_Out), .sel(or_1_out));
  or or_1 (or_1_out, or_2_out[0], or_2_out[1], or_2_out[2], or_2_out[3]);
  Decoder_part #(.select(4), .enable("false")) decoder_1 (
    .out0(decoder_1_out0[0]), .out1(decoder_1_out0[1]), .out2(decoder_1_out0[2]), .out3(decoder_1_out0[3]),
    .out4(decoder_1_out0[4]), .out5(decoder_1_out0[5]), .out6(decoder_1_out0[6]), .out7(decoder_1_out0[7]),
    .out8(decoder_1_out0[8]), .out9(decoder_1_out0[9]), .out10(decoder_1_out0[10]),
    .out11(decoder_1_out0[11]), .out12(decoder_1_out0[12]), .out13(decoder_1_out0[13]),
    .out14(decoder_1_out0[14]), .out15(decoder_1_out0[15]), .sel(IR_In[3:0]));
  assign or_2_out = IR_In[7:4] | IR_In[11:8] | IR_In[15:12] | IR_In[19:16] | IR_In[23:20] | IR_In[27:24] | IR_In[31:28];  // OR_Gate or_2, 4 bits wide

  assign Debug_Instruction = IR_In[3:0];

  // Notes on the sheet:
  //   Cory Mollenhour
  //   CLA8
endmodule

module Timer (
  input  Clock,
  input  Stop,
  input  Clear,
  output [7:0] T_Out
);

  wire [2:0] sc_1_seq_out;
  wire [7:0] decoder_1_out0;

  Multiplexer #(.width(8), .enable("false")) multiplexer_1 (
    .in0(decoder_1_out0), .in1({8{1'b0}}), .out(T_Out), .sel(Stop));
  Decoder_part #(.select(3), .enable("false")) decoder_1 (
    .out0(decoder_1_out0[0]), .out1(decoder_1_out0[1]), .out2(decoder_1_out0[2]), .out3(decoder_1_out0[3]),
    .out4(decoder_1_out0[4]), .out5(decoder_1_out0[5]), .out6(decoder_1_out0[6]), .out7(decoder_1_out0[7]),
    .sel(sc_1_seq_out));
  SC sc_1 (.Clock(Clock), .Clear(Clear), .SEQ_out(sc_1_seq_out));

  // Notes on the sheet:
  //   Cory Mollenhour
  //   CLA8
endmodule

module RSC (
  input  in_1
);

  wire control_1_acc_bus, control_1_acc_clr, control_1_acc_ld, control_1_ar_ld, control_1_dr_bus,
       control_1_dr_ld, control_1_ir_ld, control_1_outr_ld, control_1_pc_bus, control_1_pc_inc,
       control_1_pc_ld, control_1_r_bus, control_1_r_ld, control_1_ram_en, control_1_ram_r_prime_w,
       Primary_Clock_out, z_reg_1_z_out;
  wire [2:0] control_1_alu_s;
  wire [31:0] acc_1_output, alu_1_alu_out, ar_1_output, dr_1_output, ir_1_output, outr_1_output, r_1_bus_out;

  Clock Primary_Clock (.out(Primary_Clock_out));
  OUTR outr_1 (.Input(r_1_bus_out), .Clock(Primary_Clock_out), .Load(control_1_outr_ld), .Output(outr_1_output));
  R r_1 (
    .Input(r_1_bus_out), .Clock(Primary_Clock_out), .Load(control_1_r_ld), .Bus(control_1_r_bus),
    .Bus_Out(r_1_bus_out));  // open: Output
  ALU alu_1 (
    .A(acc_1_output), .B(r_1_bus_out), .S2(control_1_alu_s[2]), .S1(control_1_alu_s[1]),
    .S0(control_1_alu_s[0]), .ALU_Out(alu_1_alu_out));
  Hex_Digit_Display hex_digit_display_1 (.value(outr_1_output[31:28]));  // open: dp
  AR ar_1 (.Input(r_1_bus_out), .Clock(Primary_Clock_out), .Load(control_1_ar_ld), .Output(ar_1_output));
  Hex_Digit_Display hex_digit_display_2 (.value(outr_1_output[23:20]));  // open: dp
  Hex_Digit_Display hex_digit_display_3 (.value(outr_1_output[27:24]));  // open: dp
  DR dr_1 (
    .Input(r_1_bus_out), .Clock(Primary_Clock_out), .Load(control_1_dr_ld), .Bus(control_1_dr_bus),
    .Output(dr_1_output), .Bus_Out(r_1_bus_out));
  Hex_Digit_Display hex_digit_display_4 (.value(outr_1_output[19:16]));  // open: dp
  PC pc_1 (
    .Input(r_1_bus_out), .Clock(Primary_Clock_out), .Load(control_1_pc_ld), .Count(control_1_pc_inc),
    .Bus(control_1_pc_bus), .Bus_Out(r_1_bus_out));  // open: Output
  ACC acc_1 (
    .Input(alu_1_alu_out), .Clock(Primary_Clock_out), .Load(control_1_acc_ld), .Clear(control_1_acc_clr),
    .Bus(control_1_acc_bus), .Output(acc_1_output), .Bus_Out(r_1_bus_out));
  Hex_Digit_Display hex_digit_display_5 (.value(outr_1_output[15:12]));  // open: dp
  Hex_Digit_Display hex_digit_display_6 (.value(outr_1_output[11:8]));  // open: dp
  RAM #(.addrWidth(16), .dataWidth(32)) ram_1 (
    .addr(ar_1_output[15:0]), .data(r_1_bus_out), .sel(control_1_ram_en), .clk(Primary_Clock_out),
    .ld(control_1_ram_r_prime_w), .clr(in_1));
  Hex_Digit_Display hex_digit_display_7 (.value(outr_1_output[3:0]));  // open: dp
  Hex_Digit_Display hex_digit_display_8 (.value(outr_1_output[7:4]));  // open: dp
  IR ir_1 (.Input(dr_1_output), .Clock(Primary_Clock_out), .Load(control_1_ir_ld), .Output(ir_1_output));
  Control control_1 (
    .RAM_R_prime_W(control_1_ram_r_prime_w), .RAM_EN(control_1_ram_en), .AR_LD(control_1_ar_ld),
    .PC_BUS(control_1_pc_bus), .PC_INC(control_1_pc_inc), .PC_LD(control_1_pc_ld), .DR_BUS(control_1_dr_bus),
    .DR_LD(control_1_dr_ld), .R_BUS(control_1_r_bus), .R_LD(control_1_r_ld), .ACC_BUS(control_1_acc_bus),
    .ACC_CLR(control_1_acc_clr), .ACC_LD(control_1_acc_ld), .ALU_S(control_1_alu_s),
    .OUTR_LD(control_1_outr_ld), .IR_LD(control_1_ir_ld), .Clock(Primary_Clock_out), .Z_In(z_reg_1_z_out),
    .IR_In(ir_1_output));  // open: Z_LD, T, D
  Z_Reg z_reg_1 (.ACC_In(acc_1_output), .Clock(Primary_Clock_out), .Load(control_1_acc_ld), .Z_out(z_reg_1_z_out));

  // Notes on the sheet:
  //   Cory Mollenhour
  //   OLA 7
endmodule

module Z_Reg (
  input  Clock,
  input  [31:0] ACC_In,
  input  Load,
  output Z_out
);

  wire nor_1_out;

  nor nor_1 (nor_1_out, ACC_In[0], ACC_In[1], ACC_In[2], ACC_In[3], ACC_In[4], ACC_In[5], ACC_In[6], ACC_In[7], ACC_In[8], ACC_In[9], ACC_In[10], ACC_In[11], ACC_In[12], ACC_In[13], ACC_In[14], ACC_In[15], ACC_In[16], ACC_In[17], ACC_In[18], ACC_In[19], ACC_In[20], ACC_In[21], ACC_In[22], ACC_In[23], ACC_In[24], ACC_In[25], ACC_In[26], ACC_In[27], ACC_In[28], ACC_In[29], ACC_In[30], ACC_In[31]);
  _1bit_reg u_1bit_reg_1 (.Data(nor_1_out), .Clock(Clock), .Load(Load), .Clear(1'b0), .Data_out(Z_out));

  // Notes on the sheet:
  //   Cory Mollenhour
  //   OLA 7
endmodule

module _1bit_reg (
  input  Clock,
  input  Data,
  input  Clear,
  input  Load,
  output Data_out
);

  wire and_1_out, and_2_out, not_1_out, not_2_out;

  and and_1 (and_1_out, Data, Load);
  not not_1 (not_1_out, Data);
  and and_2 (and_2_out, not_1_out, Load);
  J_K_Flip_Flop j_k_ff_1 (
    .J(and_1_out), .clk(Clock), .K(and_2_out), .Q(Data_out), .preset(1'b0), .en(not_2_out), .reset(Clear));  // open: Qn
  not not_2 (not_2_out, Clear);

  // Notes on the sheet:
  //   Cory Mollenhour
  //   OLA 7
endmodule

module Control (
  input  Clock,
  input  [31:0] IR_In,
  input  Z_In,
  output IR_LD,
  output [7:0] T,
  output RAM_R_prime_W,
  output RAM_EN,
  output [3:0] D,
  output AR_LD,
  output PC_BUS,
  output PC_INC,
  output PC_LD,
  output DR_BUS,
  output DR_LD,
  output R_BUS,
  output R_LD,
  output ACC_BUS,
  output ACC_CLR,
  output ACC_LD,
  output [2:0] ALU_S,
  output OUTR_LD,
  output Z_LD
);

  wire S_data_out;
  wire [15:0] decoder_1_d_out;

  IR_LD ir_ld_1 (.t2(T[2]), .clock(Clock), .IR_LD(IR_LD));
  RAM_RW ram_rw_1 (
    .t1(T[1]), .t3(T[3]), .t5(T[5]), .d1(decoder_1_d_out[1]), .d2(decoder_1_d_out[2]),
    .d5(decoder_1_d_out[5]), .d6(decoder_1_d_out[6]), .z(Z_In), .RAM_RW(RAM_R_prime_W));
  RAM_EN ram_en_1 (
    .t1(T[1]), .t3(T[3]), .t5(T[5]), .t6(T[6]), .d1(decoder_1_d_out[1]), .d2(decoder_1_d_out[2]),
    .d5(decoder_1_d_out[5]), .d6(decoder_1_d_out[6]), .z(Z_In), .RAM_EN(RAM_EN));
  AR_LD ar_ld_1 (
    .t0(T[0]), .t2(T[2]), .t4(T[4]), .clock(Clock), .d1(decoder_1_d_out[1]), .d2(decoder_1_d_out[2]),
    .AR_LD(AR_LD));
  PC_BUS pc_bus_1 (.t0(T[0]), .t2(T[2]), .PC_BUS(PC_BUS));
  PC_INC pc_inc_1 (
    .t1(T[1]), .t3(T[3]), .clock(Clock), .d1(decoder_1_d_out[1]), .d2(decoder_1_d_out[2]),
    .d6(decoder_1_d_out[6]), .z(Z_In), .PC_INC(PC_INC));
  PC_LD pc_ld_1 (.t4(T[4]), .clock(Clock), .d5(decoder_1_d_out[5]), .d6(decoder_1_d_out[6]), .z(Z_In), .PC_LD(PC_LD));
  DR_BUS dr_bus_1 (
    .t4(T[4]), .t6(T[6]), .d1(decoder_1_d_out[1]), .d2(decoder_1_d_out[2]), .d5(decoder_1_d_out[5]),
    .d6(decoder_1_d_out[6]), .z(Z_In), .DR_BUS(DR_BUS));
  DR_LD dr_ld_1 (
    .t1(T[1]), .t3(T[3]), .t5(T[5]), .clock(Clock), .d1(decoder_1_d_out[1]), .d2(decoder_1_d_out[2]),
    .d5(decoder_1_d_out[5]), .d6(decoder_1_d_out[6]), .z(Z_In), .DR_LD(DR_LD));
  R_BUS r_bus_1 (
    .t3(T[3]), .d4(decoder_1_d_out[4]), .d8(decoder_1_d_out[8]), .d9(decoder_1_d_out[9]),
    .d12(decoder_1_d_out[12]), .d13(decoder_1_d_out[13]), .R_BUS(R_BUS));
  R_LD r_ld_1 (.t3(T[3]), .clock(Clock), .d3(decoder_1_d_out[3]), .R_LD(R_LD));
  ACC_BUS acc_bus_1 (
    .t3(T[3]), .t5(T[5]), .d2(decoder_1_d_out[2]), .d3(decoder_1_d_out[3]), .d7(decoder_1_d_out[7]),
    .ACC_BUS(ACC_BUS));
  ACC_CLR acc_clr_1 (.t3(T[3]), .d11(decoder_1_d_out[11]), .ACC_CLR(ACC_CLR));
  ACC_LD acc_ld_1 (
    .t3(T[3]), .t6(T[6]), .clock(Clock), .d1(decoder_1_d_out[1]), .d4(decoder_1_d_out[4]),
    .d8(decoder_1_d_out[8]), .d9(decoder_1_d_out[9]), .d10(decoder_1_d_out[10]), .d12(decoder_1_d_out[12]),
    .d13(decoder_1_d_out[13]), .d14(decoder_1_d_out[14]), .d15(decoder_1_d_out[15]), .ACC_LD(ACC_LD));
  ALU_SEL alu_sel_1 (
    .d1(decoder_1_d_out[1]), .d4(decoder_1_d_out[4]), .d9(decoder_1_d_out[9]), .d10(decoder_1_d_out[10]),
    .d12(decoder_1_d_out[12]), .d13(decoder_1_d_out[13]), .d14(decoder_1_d_out[14]),
    .d15(decoder_1_d_out[15]), .S2(ALU_S[2]), .S1(ALU_S[1]), .S0(ALU_S[0]));
  OUTR_LD outr_ld_1 (.t3(T[3]), .clock(Clock), .d7(decoder_1_d_out[7]), .OUTR_LD(OUTR_LD));
  Z_LD z_ld_1 (.clock(Clock), .Z_LD(Z_LD));
  Timer timer_1 (.T_Out(T), .Clock(Clock), .Stop(S_data_out));  // open: Clear
  _1bit_reg S (.Data(1'b1), .Clock(Clock), .Clear(1'b0), .Data_out(S_data_out));  // open: Load
  Decoder decoder_1 (.D_Out(decoder_1_d_out), .Debug_Instruction(D), .IR_In(IR_In));

  // Notes on the sheet:
  //   Cory Mollenhour
  //   OLA 7
  //   0  1   2   3        4   5   6   7
  //   T Signals
  //   0  1   2   3        4   5   6   7       8   9 10  11    12 13 14 15               z
endmodule
